# Fritzing sketch Schematic (saved by Fritzing 0.8.7b)
circuit board: 8.66012cm x 5.72735cm
breadboards: 1

parts:
  The_Brains = Arduino Nano (Rev3.0)
  V1 = DC Power [voltage=5]
  Q1 = MOSFET-NCHANNEL [package=to220v]
  R1 = Resistor [tolerance=±5% resistance=1k package=THT]
  D1 = Rectifier Diode [part_number=1N4001 package="300 mil [THT]"]
  C1 = Tantalum Capacitor [capacitance=1μF package="100 mil [THT, tantalum]"]
  D2 = Rectifier Diode [part_number=1N4001 package="300 mil [THT]"]
  JP1 = Header 4 [package=jst-4-pth]
  IC1 = ULN2003A [package="DIP16 [THT]"]
  U1 = POT [package=trim_pot]
  U2 = POT [package=trim_pot]
  C4 = Tantalum Capacitor [capacitance=1μF package="100 mil [THT, tantalum]"]
  C6 = Tantalum Capacitor [capacitance=1μF package="100 mil [THT, tantalum]"]
  C7 = Tantalum Capacitor [capacitance=1μF package="100 mil [THT, tantalum]"]
  JP2 = Header 5 [package=1x05-1mm]
  JP3 = Header 2 [package=springterminal-2.54mm-2]

nets:
  N1: The_Brains.GND, V1.V-, Q1.S, D1.cathode, JP1.1, U1.E, U2.E, C4.-, C6.-, C7.-
  N2: The_Brains.D3, R1.Pin_0
  N3: The_Brains.D8, IC1.In_4
  N4: The_Brains.D9, IC1.In_3
  N5: The_Brains.D10, IC1.In_2
  N6: The_Brains.D11/MOSI, IC1.In_1
  N7: The_Brains.5V, V1.V+, D2.anode, JP1.2, U1.A, U2.A, C4.+, JP3.1
  N8: The_Brains.A5, JP1.4
  N9: The_Brains.A4, JP1.3
  N10: The_Brains.A1, U2.S, C7.+
  N11: The_Brains.A0, U1.S, C6.+
  N12: Q1.G, R1.Pin_1
  N13: Q1.D, JP3.2
  N14: D1.anode, C1.-, IC1.0V
  N15: C1.+, D2.cathode, IC1.COM_-_Common, JP2.5
  N16: IC1.Out_4, JP2.4
  N17: IC1.Out_3, JP2.3
  N18: IC1.Out_2, JP2.2
  N19: IC1.Out_1, JP2.1

notes:
  I2C LCD
  To 28BYJ-48 Stepper
  Type 130 12V Motor
